// Logisim project rv.circ as structural Verilog: 1 circuit, main circuit main
module main (
  input  in_1
);

  wire clock_1_out, main_1_p3, main_1_p4, main_1_p5, main_1_p6, main_1_p7, main_1_p8, main_2_p6, main_2_p7,
       main_2_p8, main_3_p2, main_3_p3, main_3_p4, main_3_p5, main_3_p6, main_3_p7, main_3_p8, main_4_p4,
       main_4_p10, main_5_p8;
  wire [23:0] main_2_p5;
  wire [31:0] adder_1_out, main_1_p1, main_2_p1, main_4_p11, ram_1_data, register_1_q;
  wire [31:24] main_2_p5_2;

  Register #(.width(32)) register_1 (.D(main_2_p1), .Q(register_1_q), .clk(clock_1_out), .clr(in_1));  // open: en
  Clock clock_1 (.out(clock_1_out));
  // bit_extender_main main_1: pin names not known; wires that end beside it: main_1_p1, register_1_q, main_1_p3, main_1_p4, main_1_p5, main_1_p6, main_1_p7, main_1_p8
  Adder #(.width(32)) adder_1 (.a(32'h4), .b(register_1_q), .out(adder_1_out));  // open: cin, cout
  // pc_control_main main_2: pin names not known; wires that end beside it: main_2_p1, adder_1_out, main_1_p8, main_1_p5, {main_2_p5_2, main_2_p5}, main_2_p6, main_2_p7, main_2_p8
  ROM #(.addrWidth(20), .dataWidth(32)) rom_1 (.addr(register_1_q[21:2]), .data(main_1_p1));  // open: sel
  // Probe on main_1_p1[6:0]
  // Probe on main_1_p1[14:12]
  // Probe on main_1_p1[19:15]
  // Probe on main_1_p1[11:7]
  // Probe on main_1_p1[24:20]
  // Probe on main_4_p4
  // Comtrol_main main_3: pin names not known; wires that end beside it: main_1_p1[6:0], main_3_p2, main_3_p3, main_3_p4, main_3_p5, main_3_p6, main_3_p7, main_3_p8
  // regfile_main main_4: pin names not known; wires that end beside it: main_1_p1[11:7], main_1_p1[19:15], main_1_p1[24:20], main_4_p4, main_2_p7, main_2_p6, main_3_p2, in_1, clock_1_out, main_4_p10, main_4_p11
  // input_control_main main_5: pin names not known; wires that end beside it: main_4_p11, main_1_p3, main_1_p4, main_3_p3, main_3_p4, main_2_p6, main_2_p7, main_5_p8, main_5_p8, main_3_p6, main_2_p8, {main_2_p5_2, main_2_p5}
  // ALU alu_1: pin names not known; wires that end beside it: main_4_p10, main_3_p4, main_1_p1[30], main_1_p1[14:12]
  RAM #(.addrWidth(24), .dataWidth(32), .bus("separate")) ram_1 (
    .addr(main_2_p5), .din(main_4_p11), .data(ram_1_data), .str(main_3_p4), .clk(clock_1_out),
    .ld(main_3_p5), .clr(in_1));  // open: sel
  // out_control_main main_6: pin names not known; wires that end beside it: main_4_p4, main_2_p6, main_2_p7, main_3_p8, main_3_p7, main_3_p5, {main_2_p5_2, main_2_p5}, ram_1_data, main_1_p6, main_1_p7, adder_1_out

  // Notes on the sheet:
  //   contents of rom_1 (hex, n*v repeats v):
  //   5537 33 33 33 4080ef 8080e7
endmodule
